// Logisim project CRC.circ as structural Verilog: 2 circuits, main circuit CRC
module CRC (
  input  [7:0] Data,
  input  [3:0] Divider,
  output [10:0] out_3
);

  wire [2:0] div_1_remainder, div_2_remainder, div_3_remainder, div_4_remainder, div_5_remainder,
       div_6_remainder, div_7_remainder;

  // Probe on Data[7:4]
  // Probe on {div_1_remainder, Data[3]}
  div div_1 (.Divisor(Divider), .Divident(Data[7:4]), .Remainder(div_1_remainder));
  div div_2 (.Divisor(Divider), .Divident({div_1_remainder, Data[3]}), .Remainder(div_2_remainder));
  // Probe on {div_2_remainder, Data[2]}
  div div_3 (.Divisor(Divider), .Divident({div_2_remainder, Data[2]}), .Remainder(div_3_remainder));
  // Probe on {div_3_remainder, Data[1]}
  div div_4 (.Divisor(Divider), .Divident({div_3_remainder, Data[1]}), .Remainder(div_4_remainder));
  // Probe on {div_4_remainder, Data[0]}
  div div_5 (.Divisor(Divider), .Divident({div_4_remainder, Data[0]}), .Remainder(div_5_remainder));
  // Probe on {div_5_remainder, 1'b0}
  div div_6 (.Divisor(Divider), .Divident({div_5_remainder, 1'b0}), .Remainder(div_6_remainder));
  // Probe on {div_6_remainder, 1'b0}
  // Probe on {div_7_remainder, 1'b0}
  div div_7 (.Divisor(Divider), .Divident({div_6_remainder, 1'b0}), .Remainder(div_7_remainder));
  div div_8 (.Divisor(Divider), .Divident({div_7_remainder, 1'b0}), .Remainder(out_3[2:0]));

  assign out_3[10:3] = Data;
endmodule

module div (
  input  [3:0] Divisor,
  input  [3:0] Divident,
  output [2:0] Remainder
);

  wire comparator_1_lt;
  wire [3:0] xor_1_out;
  wire [3:3] multiplexer_1_out;

  assign xor_1_out = Divisor ^ Divident;  // XOR_Gate xor_1, 4 bits wide
  Multiplexer #(.width(4)) multiplexer_1 (
    .in0(xor_1_out), .in1(Divident), .out({multiplexer_1_out[3], Remainder}), .sel(comparator_1_lt));  // open: en
  Comparator #(.width(4), .mode("unsigned")) comparator_1 (
    .a(Divident), .b(4'b1000), .lt(comparator_1_lt));  // open: gt, eq
endmodule
