// Logisim project ftoi.circ as structural Verilog: 1 circuit, main circuit ftoi
module ftoi (
  input  [15:0] float,
  output [31:0] \int 
);

  wire comparator_1_lt, comparator_2_eq, or_1_out;
  wire [4:0] subtractor_1_out;
  wire [31:0] multiplexer_1_out, negator_1_out, shifter_1_out, shifter_2_out;

  // Probe on {16'h1, float[9:0], {6{1'b0}}}
  Comparator #(.width(5), .mode("unsigned")) comparator_1 (
    .a(float[14:10]), .b(5'b01111), .lt(comparator_1_lt));  // open: gt, eq
  Shifter #(.width(32)) shifter_1 (.in({16'h1, float[9:0], {6{1'b0}}}), .\dist (subtractor_1_out), .out(shifter_1_out));
  Subtractor #(.width(5)) subtractor_1 (.a(float[14:10]), .b(5'b01111), .out(subtractor_1_out));  // open: bin, bout
  Comparator #(.width(5), .mode("unsigned")) comparator_2 (
    .a(float[14:10]), .b({5{1'b1}}), .eq(comparator_2_eq));  // open: gt, lt
  or or_1 (or_1_out, comparator_2_eq, comparator_1_lt);
  Shifter #(.width(32), .shift("lr")) shifter_2 (.in(shifter_1_out), .\dist (5'b10000), .out(shifter_2_out));
  Negator #(.width(32)) negator_1 (.in(shifter_2_out), .out(negator_1_out));
  Multiplexer #(.width(32)) multiplexer_1 (
    .in0(shifter_2_out), .in1(negator_1_out), .out(multiplexer_1_out), .sel(float[15]));  // open: en
  // Probe on \int 
  Multiplexer #(.width(32)) multiplexer_2 (
    .in0(multiplexer_1_out), .in1({32{1'b0}}), .out(\int ), .sel(or_1_out));  // open: en
endmodule
