// Logisim project navigation.circ as structural Verilog: 2 circuits, main circuit navigation
module navigation (
  input  [1:0] dir,
  input  clk,
  input  reset,
  output arrive,
  output hit
);

  wire comparator_2_eq;
  wire [2:0] calc_1_t, register_1_q;

  Register #(.width(3)) register_1 (.D(calc_1_t), .Q(register_1_q), .clk(clk), .clr(reset));  // open: en
  calc calc_1 (.S(register_1_q), .D(dir), .T(calc_1_t));
  Comparator #(.width(3), .mode("unsigned")) comparator_1 (.a(3'b100), .b(register_1_q), .eq(arrive));  // open: gt, lt
  Register #(.width(1)) register_2 (.D(comparator_2_eq), .Q(hit), .clk(clk), .clr(reset));  // open: en
  Comparator #(.width(3), .mode("unsigned")) comparator_2 (
    .a(calc_1_t), .b(register_1_q), .eq(comparator_2_eq));  // open: gt, lt
endmodule

module calc (
  input  [2:0] S,
  input  [1:0] D,
  output [2:0] T
);

  wire and_1_out, and_2_out, and_3_out, and_4_out, and_5_out, and_6_out, and_7_out, and_8_out, and_9_out,
       and_10_out, and_11_out, and_12_out, and_13_out, not_1_out, not_2_out, not_3_out, not_4_out, not_5_out,
       not_6_out, not_7_out, not_8_out, not_9_out, not_10_out, not_11_out, not_12_out, not_13_out,
       not_14_out, not_15_out, not_16_out, not_17_out;

  not not_1 (not_1_out, S[0]);
  not not_2 (not_2_out, D[1]);
  not not_3 (not_3_out, D[0]);
  not not_4 (not_4_out, D[1]);
  not not_5 (not_5_out, S[1]);
  not not_6 (not_6_out, D[1]);
  not not_7 (not_7_out, D[1]);
  not not_8 (not_8_out, D[0]);
  not not_9 (not_9_out, S[0]);
  not not_10 (not_10_out, D[1]);
  not not_11 (not_11_out, S[0]);
  not not_12 (not_12_out, D[0]);
  not not_13 (not_13_out, S[2]);
  not not_14 (not_14_out, S[1]);
  not not_15 (not_15_out, D[1]);
  not not_16 (not_16_out, D[0]);
  not not_17 (not_17_out, D[0]);
  and and_1 (and_1_out, S[1], not_1_out, not_2_out, not_3_out);
  and and_2 (and_2_out, S[1], S[0], not_4_out, D[0]);
  and and_3 (and_3_out, S[2], S[1]);
  and and_4 (and_4_out, not_5_out, S[0], not_6_out);
  and and_5 (and_5_out, S[0], not_7_out, not_8_out);
  and and_6 (and_6_out, S[1], not_9_out, not_10_out, D[0]);
  and and_7 (and_7_out, S[1], not_11_out, D[1], not_12_out);
  and and_8 (and_8_out, S[1], S[0], D[1], D[0]);
  and and_9 (and_9_out, S[2], S[1]);
  and and_10 (and_10_out, not_13_out, not_14_out, not_15_out, not_16_out);
  and and_11 (and_11_out, S[0], D[1], D[0]);
  and and_12 (and_12_out, S[1], D[1], D[0]);
  and and_13 (and_13_out, S[1], S[0], not_17_out);
  or or_1 (T[2], and_1_out, and_2_out, and_3_out);
  or or_2 (T[1], and_4_out, and_5_out, and_6_out, and_7_out, and_8_out, and_9_out);
  or or_3 (T[0], and_10_out, and_11_out, and_12_out, and_13_out);
endmodule
