// Logisim project P3-test.circ as structural Verilog: 1 circuit, main circuit main
module main (
  output [31:0] Instr,
  output RegWrite,
  output [4:0] RegAddr,
  output halt,
  output [31:0] RegData,
  output MemWrite,
  output [4:0] MemAddr,
  output [31:0] MemData
);

  wire clock_1_out, comparator_1_eq;
  wire [4:0] bit_extender_1_out, bit_extender_3_out, main_1_memaddr, main_1_regaddr;
  wire [5:0] counter_1_q;
  wire [31:0] bit_extender_2_out, bit_extender_4_out, main_1_memdata, main_1_regdata;

  Counter #(.width(6), .max('h20), .ongoal("stay")) counter_1 (
    .Q(counter_1_q), .carry(halt), .clk(clock_1_out));  // open: load, D, count, clr
  Clock clock_1 (.out(clock_1_out));
  Comparator #(.width(6), .mode("unsigned")) comparator_1 (
    .a(counter_1_q), .b({6{1'b0}}), .eq(comparator_1_eq));  // open: gt, lt
  P3_main main_1 (
    .Reset(comparator_1_eq), .Instr(Instr), .RegWrite(RegWrite), .RegAddr(main_1_regaddr),
    .RegData(main_1_regdata), .MemWrite(MemWrite), .MemAddr(main_1_memaddr), .MemData(main_1_memdata));
  assign bit_extender_1_out = {{4{RegWrite}}, RegWrite};  // Bit_Extender bit_extender_1
  assign bit_extender_2_out = {{31{RegWrite}}, RegWrite};  // Bit_Extender bit_extender_2
  assign bit_extender_3_out = {{4{MemWrite}}, MemWrite};  // Bit_Extender bit_extender_3
  assign bit_extender_4_out = {{31{MemWrite}}, MemWrite};  // Bit_Extender bit_extender_4
  assign RegAddr = bit_extender_1_out & main_1_regaddr;  // AND_Gate and_1, 5 bits wide
  assign RegData = bit_extender_2_out & main_1_regdata;  // AND_Gate and_2, 32 bits wide
  assign MemAddr = bit_extender_3_out & main_1_memaddr;  // AND_Gate and_3, 5 bits wide
  assign MemData = bit_extender_4_out & main_1_memdata;  // AND_Gate and_4, 32 bits wide
endmodule
