// Logisim project P3.circ as structural Verilog: 6 circuits, main circuit main
module main (
  input  Reset,
  output [31:0] Instr,
  output RegWrite,
  output [4:0] RegAddr,
  output [31:0] RegData,
  output MemWrite,
  output [4:0] MemAddr,
  output [31:0] MemData
);

  wire ALUSrc, and_1_out, BranchEnable, clock_1_out, ExtOp, Mem2Reg, RegDst;
  wire [2:0] ALUOp;
  wire [31:0] ALUOut, ExtOut, GRFOut0, MemOut, multiplexer_3_out;

  IFU ifu_1 (.Reset(Reset), .BranchEnable(and_1_out), .Instr(Instr));
  and and_1 (and_1_out, BranchEnable, ALUOut[0]);
  Extender extender_1 (.In(Instr[15:0]), .Op(ExtOp), .Out(ExtOut));
  Multiplexer #(.width(5)) multiplexer_1 (
    .in0(Instr[15:11]), .in1(Instr[20:16]), .out(RegAddr), .sel(RegDst));  // open: en
  Multiplexer #(.width(32)) multiplexer_2 (
    .in0({ALUOut[31:7], MemAddr, ALUOut[1:0]}), .in1(MemOut), .out(RegData), .sel(Mem2Reg));  // open: en
  GRF grf_1 (
    .Reset(Reset), .WriteEnable(RegWrite), .ReadAddr0(Instr[25:21]), .ReadAddr1(Instr[20:16]),
    .WriteAddr(RegAddr), .WriteData(RegData), .ReadData0(GRFOut0), .ReadData1(MemData));
  // Probe on Instr[15:0]
  // Probe on Instr[31:26]
  // Probe on Instr[5:0]
  // Probe on ALUOp
  Controller controller_1 (
    .Op(Instr[31:26]), .Function(Instr[5:0]), .RegDst(RegDst), .ALUSrc(ALUSrc), .Mem2Reg(Mem2Reg),
    .RegWrite(RegWrite), .MemWrite(MemWrite), .BranchEnable(BranchEnable), .ExtOp(ExtOp), .ALUOp(ALUOp));
  Multiplexer #(.width(32)) multiplexer_3 (
    .in0(MemData), .in1(ExtOut), .out(multiplexer_3_out), .sel(ALUSrc));  // open: en
  Clock clock_1 (.out(clock_1_out));
  ALU alu_1 (.Input0(GRFOut0), .Input1(multiplexer_3_out), .Op(ALUOp), .out_4({ALUOut[31:7], MemAddr, ALUOut[1:0]}));
  RAM #(.addrWidth(5), .dataWidth(32), .bus("separate")) ram_1 (
    .addr(MemAddr), .din(MemData), .data(MemOut), .str(MemWrite), .clk(clock_1_out), .clr(Reset));  // open: sel, ld

  // Other names for the same wires on the sheet: ALUOut[6:2] = MemAddr; GRFOut1[31:0] = MemData;
  //   Function[5:0] = Instr[5:0]; imm[15:0] = Instr[15:0]; rd[4:0] = Instr[15:11]; rt[4:0] = Instr[20:16];
  //   rs[4:0] = Instr[25:21]; Op[5:0] = Instr[31:26]
endmodule

module GRF (
  input  Reset,
  input  WriteEnable,
  input  [4:0] ReadAddr0,
  input  [4:0] ReadAddr1,
  input  [4:0] WriteAddr,
  input  [31:0] WriteData,
  output [31:0] ReadData0,
  output [31:0] ReadData1
);

  wire clock_1_out, decoder_1_out1, decoder_1_out2, decoder_1_out3, decoder_1_out4, decoder_1_out5,
       decoder_1_out6, decoder_1_out7, decoder_1_out8, decoder_1_out9, decoder_1_out10, decoder_1_out11,
       decoder_1_out12, decoder_1_out13, decoder_1_out14, decoder_1_out15, decoder_1_out16, decoder_1_out17,
       decoder_1_out18, decoder_1_out19, decoder_1_out20, decoder_1_out21, decoder_1_out22, decoder_1_out23,
       decoder_1_out24, decoder_1_out25, decoder_1_out26, decoder_1_out27, decoder_1_out28, decoder_1_out29,
       decoder_1_out30, decoder_1_out31;
  wire [31:0] register_1_q, register_2_q, register_3_q, register_4_q, register_5_q, register_6_q,
       register_7_q, register_8_q, register_9_q, register_10_q, register_11_q, register_12_q, register_13_q,
       register_14_q, register_15_q, register_16_q, register_17_q, register_18_q, register_19_q,
       register_20_q, register_21_q, register_22_q, register_23_q, register_24_q, register_25_q,
       register_26_q, register_27_q, register_28_q, register_29_q, register_30_q, register_31_q;

  Clock clock_1 (.out(clock_1_out));
  Decoder #(.select(5), .disabled(0)) decoder_1 (
    .out1(decoder_1_out1), .out2(decoder_1_out2), .out3(decoder_1_out3), .out4(decoder_1_out4),
    .out5(decoder_1_out5), .out6(decoder_1_out6), .out7(decoder_1_out7), .out8(decoder_1_out8),
    .out9(decoder_1_out9), .out10(decoder_1_out10), .out11(decoder_1_out11), .out12(decoder_1_out12),
    .out13(decoder_1_out13), .out14(decoder_1_out14), .out15(decoder_1_out15), .out16(decoder_1_out16),
    .out17(decoder_1_out17), .out18(decoder_1_out18), .out19(decoder_1_out19), .out20(decoder_1_out20),
    .out21(decoder_1_out21), .out22(decoder_1_out22), .out23(decoder_1_out23), .out24(decoder_1_out24),
    .out25(decoder_1_out25), .out26(decoder_1_out26), .out27(decoder_1_out27), .out28(decoder_1_out28),
    .out29(decoder_1_out29), .out30(decoder_1_out30), .out31(decoder_1_out31), .sel(WriteAddr),
    .en(WriteEnable));  // open: out0
  Register #(.width(32)) register_1 (
    .D(WriteData), .en(decoder_1_out1), .Q(register_1_q), .clk(clock_1_out), .clr(Reset));
  Register #(.width(32)) register_2 (
    .D(WriteData), .en(decoder_1_out2), .Q(register_2_q), .clk(clock_1_out), .clr(Reset));
  Register #(.width(32)) register_3 (
    .D(WriteData), .en(decoder_1_out3), .Q(register_3_q), .clk(clock_1_out), .clr(Reset));
  Register #(.width(32)) register_4 (
    .D(WriteData), .en(decoder_1_out4), .Q(register_4_q), .clk(clock_1_out), .clr(Reset));
  Register #(.width(32)) register_5 (
    .D(WriteData), .en(decoder_1_out5), .Q(register_5_q), .clk(clock_1_out), .clr(Reset));
  Register #(.width(32)) register_6 (
    .D(WriteData), .en(decoder_1_out6), .Q(register_6_q), .clk(clock_1_out), .clr(Reset));
  Register #(.width(32)) register_7 (
    .D(WriteData), .en(decoder_1_out7), .Q(register_7_q), .clk(clock_1_out), .clr(Reset));
  Register #(.width(32)) register_8 (
    .D(WriteData), .en(decoder_1_out8), .Q(register_8_q), .clk(clock_1_out), .clr(Reset));
  Register #(.width(32)) register_9 (
    .D(WriteData), .en(decoder_1_out9), .Q(register_9_q), .clk(clock_1_out), .clr(Reset));
  Register #(.width(32)) register_10 (
    .D(WriteData), .en(decoder_1_out10), .Q(register_10_q), .clk(clock_1_out), .clr(Reset));
  Register #(.width(32)) register_11 (
    .D(WriteData), .en(decoder_1_out11), .Q(register_11_q), .clk(clock_1_out), .clr(Reset));
  Register #(.width(32)) register_12 (
    .D(WriteData), .en(decoder_1_out12), .Q(register_12_q), .clk(clock_1_out), .clr(Reset));
  Register #(.width(32)) register_13 (
    .D(WriteData), .en(decoder_1_out13), .Q(register_13_q), .clk(clock_1_out), .clr(Reset));
  Register #(.width(32)) register_14 (
    .D(WriteData), .en(decoder_1_out14), .Q(register_14_q), .clk(clock_1_out), .clr(Reset));
  Register #(.width(32)) register_15 (
    .D(WriteData), .en(decoder_1_out15), .Q(register_15_q), .clk(clock_1_out), .clr(Reset));
  Register #(.width(32)) register_16 (
    .D(WriteData), .en(decoder_1_out16), .Q(register_16_q), .clk(clock_1_out), .clr(Reset));
  Register #(.width(32)) register_17 (
    .D(WriteData), .en(decoder_1_out17), .Q(register_17_q), .clk(clock_1_out), .clr(Reset));
  Register #(.width(32)) register_18 (
    .D(WriteData), .en(decoder_1_out18), .Q(register_18_q), .clk(clock_1_out), .clr(Reset));
  Register #(.width(32)) register_19 (
    .D(WriteData), .en(decoder_1_out19), .Q(register_19_q), .clk(clock_1_out), .clr(Reset));
  Register #(.width(32)) register_20 (
    .D(WriteData), .en(decoder_1_out20), .Q(register_20_q), .clk(clock_1_out), .clr(Reset));
  Register #(.width(32)) register_21 (
    .D(WriteData), .en(decoder_1_out21), .Q(register_21_q), .clk(clock_1_out), .clr(Reset));
  Register #(.width(32)) register_22 (
    .D(WriteData), .en(decoder_1_out22), .Q(register_22_q), .clk(clock_1_out), .clr(Reset));
  Register #(.width(32)) register_23 (
    .D(WriteData), .en(decoder_1_out23), .Q(register_23_q), .clk(clock_1_out), .clr(Reset));
  Register #(.width(32)) register_24 (
    .D(WriteData), .en(decoder_1_out24), .Q(register_24_q), .clk(clock_1_out), .clr(Reset));
  Register #(.width(32)) register_25 (
    .D(WriteData), .en(decoder_1_out25), .Q(register_25_q), .clk(clock_1_out), .clr(Reset));
  Register #(.width(32)) register_26 (
    .D(WriteData), .en(decoder_1_out26), .Q(register_26_q), .clk(clock_1_out), .clr(Reset));
  Register #(.width(32)) register_27 (
    .D(WriteData), .en(decoder_1_out27), .Q(register_27_q), .clk(clock_1_out), .clr(Reset));
  Register #(.width(32)) register_28 (
    .D(WriteData), .en(decoder_1_out28), .Q(register_28_q), .clk(clock_1_out), .clr(Reset));
  Register #(.width(32)) register_29 (
    .D(WriteData), .en(decoder_1_out29), .Q(register_29_q), .clk(clock_1_out), .clr(Reset));
  Register #(.width(32)) register_30 (
    .D(WriteData), .en(decoder_1_out30), .Q(register_30_q), .clk(clock_1_out), .clr(Reset));
  Register #(.width(32)) register_31 (
    .D(WriteData), .en(decoder_1_out31), .Q(register_31_q), .clk(clock_1_out), .clr(Reset));
  Multiplexer #(.select(5), .width(32)) multiplexer_1 (
    .in0({32{1'b0}}), .in1(register_1_q), .in2(register_2_q), .in3(register_3_q), .in4(register_4_q),
    .in5(register_5_q), .in6(register_6_q), .in7(register_7_q), .in8(register_8_q), .in9(register_9_q),
    .in10(register_10_q), .in11(register_11_q), .in12(register_12_q), .in13(register_13_q),
    .in14(register_14_q), .in15(register_15_q), .in16(register_16_q), .in17(register_17_q),
    .in18(register_18_q), .in19(register_19_q), .in20(register_20_q), .in21(register_21_q),
    .in22(register_22_q), .in23(register_23_q), .in24(register_24_q), .in25(register_25_q),
    .in26(register_26_q), .in27(register_27_q), .in28(register_28_q), .in29(register_29_q),
    .in30(register_30_q), .in31(register_31_q), .out(ReadData0), .sel(ReadAddr0));  // open: en
  Multiplexer #(.select(5), .width(32)) multiplexer_2 (
    .in0({32{1'b0}}), .in1(register_1_q), .in2(register_2_q), .in3(register_3_q), .in4(register_4_q),
    .in5(register_5_q), .in6(register_6_q), .in7(register_7_q), .in8(register_8_q), .in9(register_9_q),
    .in10(register_10_q), .in11(register_11_q), .in12(register_12_q), .in13(register_13_q),
    .in14(register_14_q), .in15(register_15_q), .in16(register_16_q), .in17(register_17_q),
    .in18(register_18_q), .in19(register_19_q), .in20(register_20_q), .in21(register_21_q),
    .in22(register_22_q), .in23(register_23_q), .in24(register_24_q), .in25(register_25_q),
    .in26(register_26_q), .in27(register_27_q), .in28(register_28_q), .in29(register_29_q),
    .in30(register_30_q), .in31(register_31_q), .out(ReadData1), .sel(ReadAddr1));  // open: en
endmodule

module ALU (
  input  [31:0] Input0,
  input  [31:0] Input1,
  input  [2:0] Op,
  output [31:0] out_4
);

  wire comparator_1_eq;
  wire [31:0] adder_1_out, bit_extender_1_out, or_1_out, shifter_1_out, subtractor_1_out;

  Adder #(.width(32)) adder_1 (.a(Input0), .b(Input1), .out(adder_1_out));  // open: cin, cout
  Subtractor #(.width(32)) subtractor_1 (.a(Input0), .b(Input1), .out(subtractor_1_out));  // open: bin, bout
  assign or_1_out = Input0 | Input1;  // OR_Gate or_1, 32 bits wide
  Comparator #(.width(32), .mode("unsigned")) comparator_1 (
    .a(Input0), .b(Input1), .eq(comparator_1_eq));  // open: gt, lt
  Shifter #(.width(32)) shifter_1 (.in(Input1), .\dist (5'b10000), .out(shifter_1_out));
  assign bit_extender_1_out = {{31{1'b0}}, comparator_1_eq};  // Bit_Extender bit_extender_1
  Multiplexer #(.select(3), .width(32)) multiplexer_1 (
    .in0(adder_1_out), .in1(subtractor_1_out), .in2(or_1_out), .in3(bit_extender_1_out), .in4(shifter_1_out),
    .out(out_4), .sel(Op));  // open: in5, in6, in7, en
endmodule

module IFU (
  input  Reset,
  input  BranchEnable,
  output [31:0] Instr
);

  wire clock_1_out;
  wire [4:0] adder_1_out, adder_2_out, multiplexer_1_out, PC_q;

  Clock clock_1 (.out(clock_1_out));
  Register #(.width(5)) PC (.D(adder_2_out), .Q(PC_q), .clk(clock_1_out), .clr(Reset));  // open: en
  RAM #(.addrWidth(5), .dataWidth(32)) ram_1 (.addr(PC_q), .data(Instr), .clk(Reset));  // open: sel, ld, clr
  Adder #(.width(5)) adder_1 (.a(PC_q), .b(5'b00001), .out(adder_1_out));  // open: cin, cout
  Multiplexer #(.width(5)) multiplexer_1 (
    .in0({5{1'b0}}), .in1(Instr[4:0]), .out(multiplexer_1_out), .sel(BranchEnable));  // open: en
  Adder #(.width(5)) adder_2 (.a(adder_1_out), .b(multiplexer_1_out), .out(adder_2_out));  // open: cin, cout
endmodule

module Controller (
  input  [5:0] Op,
  input  [5:0] Function,
  output RegDst,
  output ALUSrc,
  output Mem2Reg,
  output RegWrite,
  output MemWrite,
  output BranchEnable,
  output ExtOp,
  output [2:0] ALUOp
);

  wire addu_out, not_1_out, not_2_out, not_3_out, not_4_out, not_5_out, not_6_out, not_7_out, not_8_out,
       not_9_out, not_10_out, not_11_out, not_12_out, ori_out, subu_out;

  not not_1 (not_1_out, Function[0]);
  not not_2 (not_2_out, Function[1]);
  not not_3 (not_3_out, Function[2]);
  not not_4 (not_4_out, Function[3]);
  not not_5 (not_5_out, Function[4]);
  not not_6 (not_6_out, Function[5]);
  not not_7 (not_7_out, Op[0]);
  not not_8 (not_8_out, Op[1]);
  not not_9 (not_9_out, Op[2]);
  not not_10 (not_10_out, Op[3]);
  not not_11 (not_11_out, Op[4]);
  not not_12 (not_12_out, Op[5]);
  and addu (addu_out, not_12_out, not_11_out, not_10_out, not_9_out, not_8_out, not_7_out, Function[5], not_5_out, not_4_out, not_3_out, not_2_out, Function[0]);
  and subu (subu_out, not_12_out, not_11_out, not_10_out, not_9_out, not_8_out, not_7_out, Function[5], not_5_out, not_4_out, not_3_out, Function[1], Function[0]);
  and ori (ori_out, not_12_out, not_11_out, Op[3], Op[2], not_8_out, Op[0]);
  and lw (Mem2Reg, Op[5], not_11_out, not_10_out, not_9_out, Op[1], Op[0]);
  and sw (MemWrite, Op[5], not_11_out, Op[3], not_9_out, Op[1], Op[0]);
  and beq (BranchEnable, not_12_out, not_11_out, not_10_out, Op[2], not_8_out, not_7_out);
  and lui (ALUOp[2], not_12_out, not_11_out, Op[3], Op[2], Op[1], Op[0]);
  or or_1 (RegDst, ori_out, Mem2Reg, ALUOp[2]);
  or or_2 (ALUSrc, ori_out, Mem2Reg, MemWrite, ALUOp[2]);
  or or_3 (RegWrite, addu_out, subu_out, ori_out, Mem2Reg, ALUOp[2]);
  or or_4 (ExtOp, Mem2Reg, MemWrite);
  or or_5 (ALUOp[0], subu_out, BranchEnable);
  or or_6 (ALUOp[1], ori_out, BranchEnable);
endmodule

// Ext
module Extender (
  input  [15:0] In,
  input  Op,
  output [31:0] Out
);

  wire [31:0] bit_extender_1_out, bit_extender_2_out;

  assign bit_extender_1_out = {{16{1'b0}}, In};  // Bit_Extender bit_extender_1
  assign bit_extender_2_out = {{16{In[15]}}, In};  // Bit_Extender bit_extender_2
  Multiplexer #(.width(32)) multiplexer_1 (
    .in0(bit_extender_1_out), .in1(bit_extender_2_out), .out(Out), .sel(Op));  // open: en
endmodule
