// Logisim project fib1.circ as structural Verilog: 1 circuit, main circuit main
module main (
  input  [2:0] in_1,
  output [3:0] out_2
);

  wire clock_1_out, clock_2_out, clock_3_out, init, running;
  wire [2:0] counter_1_q;
  wire [3:0] fib_in_0, fib_in_1, fib_out_0, fib_out_1, register_1_q;

  Counter #(.width(3), .max('h7)) counter_1 (
    .count(running), .Q(counter_1_q), .clk(clock_1_out));  // open: load, D, carry, clr
  Clock clock_1 (.out(clock_1_out));
  Comparator #(.width(3), .mode("unsigned")) comparator_1 (.a(3'b000), .b(counter_1_q), .eq(init));  // open: gt, lt
  Comparator #(.width(3), .mode("unsigned")) comparator_2 (.a(counter_1_q), .b(in_1), .lt(running));  // open: gt, eq
  Register #(.width(4)) register_1 (.D(fib_in_0), .en(running), .Q(register_1_q), .clk(clock_2_out));  // open: clr
  Clock clock_2 (.out(clock_2_out));
  Register #(.width(4)) register_2 (.D(fib_in_1), .en(running), .Q(fib_out_0), .clk(clock_3_out));  // open: clr
  Clock clock_3 (.out(clock_3_out));
  Multiplexer #(.width(4), .enable("false")) multiplexer_1 (.in0(fib_out_0), .in1(4'b0000), .out(out_2), .sel(running));
  Adder #(.width(4)) adder_1 (.a(register_1_q), .b(fib_out_0), .out(fib_out_1));  // open: cin, cout
  Multiplexer #(.width(4), .enable("false")) multiplexer_2 (.in0(fib_out_0), .in1(4'b0000), .out(fib_in_0), .sel(init));
  Multiplexer #(.width(4), .enable("false")) multiplexer_3 (.in0(fib_out_1), .in1(4'b0001), .out(fib_in_1), .sel(init));
endmodule
