// Logisim project fib2.circ as structural Verilog: 5 circuits, main circuit quick_pow
module quick_pow (
  input  [31:0] in_1,
  input  [31:0] in_2,
  input  [31:0] in_3,
  input  [31:0] in_4,
  input  [31:0] in_5,
  output out_6,
  output [31:0] out_7,
  output [31:0] out_8,
  output [31:0] out_9,
  output [31:0] out_10
);

  wire and_2_out, clock_1_out, clock_2_out, clock_3_out, clock_4_out, clock_5_out, clock_6_out, clock_7_out,
       clock_8_out, clock_9_out, clock_10_out, comparator_1_gt, comparator_2_eq, counter_1_q, init,
       should_mul;
  wire [31:0] and_1_out, multiplexer_1_out, multiplexer_2_out, multiplexer_3_out, multiplexer_4_out,
       multiplexer_5_out, multiplexer_6_out, multiplexer_7_out, multiplexer_8_out, multiplexer_9_out, pow,
       r00_in, r01_in, r10_in, r11_in, shifter_1_out, t00_in, t00_out, t01_in, t01_out, t10_in, t10_out,
       t11_in, t11_out;

  Multiplexer #(.width(32), .enable("false")) multiplexer_1 (
    .in0(r00_in), .in1(32'h1), .out(multiplexer_1_out), .sel(init));
  Multiplexer #(.width(32), .enable("false")) multiplexer_2 (
    .in0(r10_in), .in1({32{1'b0}}), .out(multiplexer_2_out), .sel(init));
  Register #(.width(32)) t00 (.D(multiplexer_3_out), .en(out_6), .Q(t00_out), .clk(clock_1_out));  // open: clr
  Multiplexer #(.width(32), .enable("false")) multiplexer_3 (
    .in0(t00_in), .in1(in_1), .out(multiplexer_3_out), .sel(init));
  Clock clock_1 (.out(clock_1_out));
  Multiplexer #(.width(32), .enable("false")) multiplexer_4 (
    .in0(t10_in), .in1(in_4), .out(multiplexer_4_out), .sel(init));
  Register #(.width(32)) t10 (.D(multiplexer_4_out), .en(out_6), .Q(t10_out), .clk(clock_2_out));  // open: clr
  Clock clock_2 (.out(clock_2_out));
  Register #(.width(32)) r00 (.D(multiplexer_1_out), .en(should_mul), .Q(out_7), .clk(clock_3_out));  // open: clr
  Clock clock_3 (.out(clock_3_out));
  Register #(.width(32)) r10 (.D(multiplexer_2_out), .en(should_mul), .Q(out_9), .clk(clock_4_out));  // open: clr
  Clock clock_4 (.out(clock_4_out));
  Multiplexer #(.width(32), .enable("false")) multiplexer_5 (
    .in0(t01_in), .in1(in_2), .out(multiplexer_5_out), .sel(init));
  Clock clock_5 (.out(clock_5_out));
  Multiplexer #(.width(32), .enable("false")) multiplexer_6 (
    .in0(t11_in), .in1(in_5), .out(multiplexer_6_out), .sel(init));
  Clock clock_6 (.out(clock_6_out));
  Multiplexer #(.width(32), .enable("false")) multiplexer_7 (
    .in0(r01_in), .in1({32{1'b0}}), .out(multiplexer_7_out), .sel(init));
  Multiplexer #(.width(32), .enable("false")) multiplexer_8 (
    .in0(r11_in), .in1(32'h1), .out(multiplexer_8_out), .sel(init));
  Multiplexer #(.width(32), .enable("false")) multiplexer_9 (
    .in0(shifter_1_out), .in1(in_3), .out(multiplexer_9_out), .sel(init));
  Counter #(.width(1), .max('h1), .ongoal("stay")) counter_1 (
    .Q(counter_1_q), .clk(clock_7_out));  // open: load, D, count, carry, clr
  Clock clock_7 (.out(clock_7_out));
  Register #(.width(32)) t01 (.D(multiplexer_5_out), .en(out_6), .Q(t01_out), .clk(clock_5_out));  // open: clr
  Register #(.width(32)) t11 (.D(multiplexer_6_out), .en(out_6), .Q(t11_out), .clk(clock_6_out));  // open: clr
  Register #(.width(32)) r01 (.D(multiplexer_7_out), .en(should_mul), .Q(out_8), .clk(clock_8_out));  // open: clr
  Clock clock_8 (.out(clock_8_out));
  Register #(.width(32)) r11 (.D(multiplexer_8_out), .en(should_mul), .Q(out_10), .clk(clock_9_out));  // open: clr
  Clock clock_9 (.out(clock_9_out));
  Register #(.width(32)) register_1 (.D(multiplexer_9_out), .Q(pow), .clk(clock_10_out));  // open: en, clr
  Clock clock_10 (.out(clock_10_out));
  not not_1 (init, counter_1_q);
  Shifter #(.width(32), .shift("lr")) shifter_1 (.in(pow), .\dist (5'b00001), .out(shifter_1_out));
  assign and_1_out = pow & 32'h1;  // AND_Gate and_1, 32 bits wide
  mul2 mul2_1 (
    .in_1(t00_out), .in_2(t01_out), .in_3(t00_out), .in_4(t01_out), .in_5(t10_out), .in_6(t11_out),
    .in_7(t10_out), .in_8(t11_out), .out_9(t00_in), .out_11(t10_in), .out_10(t01_in), .out_12(t11_in));
  mul2 mul2_2 (
    .in_1(out_7), .in_2(out_8), .in_3(t00_out), .in_4(t01_out), .in_5(out_9), .in_6(out_10), .in_7(t10_out),
    .in_8(t11_out), .out_9(r00_in), .out_11(r10_in), .out_10(r01_in), .out_12(r11_in));
  Comparator #(.width(32), .mode("unsigned")) comparator_1 (
    .a(pow), .b({32{1'b0}}), .gt(comparator_1_gt));  // open: eq, lt
  Comparator #(.width(32), .mode("unsigned")) comparator_2 (
    .a(and_1_out), .b(32'h1), .eq(comparator_2_eq));  // open: gt, lt
  or or_1 (out_6, comparator_1_gt, init);
  and and_2 (and_2_out, out_6, comparator_2_eq);
  or or_2 (should_mul, and_2_out, init);
  // Probe on out_7
  // Probe on out_9
  // Probe on out_8
  // Probe on out_10

  // Other names for the same wires on the sheet: in00[31:0] = in_1; in01[31:0] = in_2; in10[31:0] = in_4;
  //   in11[31:0] = in_5; r00_out[31:0] = out_7; r01_out[31:0] = out_8; r10_out[31:0] = out_9; r11_out[31:0] = out_10;
  //   running = out_6
endmodule

module mul1 (
  input  [31:0] in_1,
  input  [31:0] in_2,
  input  [31:0] in_3,
  input  [31:0] in_4,
  input  [31:0] in_5,
  input  [31:0] in_6,
  output [31:0] out_7,
  output [31:0] out_8
);

  calc_cell calc_cell_1 (.in_1(in_1), .in_2(in_2), .in_3(in_3), .in_4(in_5), .out_5(out_7));
  calc_cell calc_cell_2 (.in_1(in_1), .in_2(in_2), .in_3(in_4), .in_4(in_6), .out_5(out_8));

  // Other names for the same wires on the sheet: a00[31:0] = in_1; a01[31:0] = in_2; b00[31:0] = in_3;
  //   b01[31:0] = in_4; b10[31:0] = in_5; b11[31:0] = in_6
endmodule

module mul2 (
  input  [31:0] in_1,
  input  [31:0] in_2,
  input  [31:0] in_3,
  input  [31:0] in_4,
  input  [31:0] in_5,
  input  [31:0] in_6,
  input  [31:0] in_7,
  input  [31:0] in_8,
  output [31:0] out_9,
  output [31:0] out_10,
  output [31:0] out_11,
  output [31:0] out_12
);

  calc_cell calc_cell_1 (.in_1(in_1), .in_2(in_2), .in_3(in_3), .in_4(in_7), .out_5(out_9));
  calc_cell calc_cell_2 (.in_1(in_1), .in_2(in_2), .in_3(in_4), .in_4(in_8), .out_5(out_11));
  calc_cell calc_cell_3 (.in_1(in_5), .in_2(in_6), .in_3(in_3), .in_4(in_7), .out_5(out_10));
  calc_cell calc_cell_4 (.in_1(in_5), .in_2(in_6), .in_3(in_4), .in_4(in_8), .out_5(out_12));

  // Other names for the same wires on the sheet: a00[31:0] = in_1; a01[31:0] = in_2; a10[31:0] = in_5;
  //   a11[31:0] = in_6; b00[31:0] = in_3; b01[31:0] = in_4; b10[31:0] = in_7; b11[31:0] = in_8
endmodule

module calc_cell (
  input  [31:0] in_1,
  input  [31:0] in_2,
  input  [31:0] in_3,
  input  [31:0] in_4,
  output [31:0] out_5
);

  wire [31:0] multiplier_1_out;

  Multiplier #(.width(32)) multiplier_1 (.a(in_1), .b(in_3), .out(multiplier_1_out));  // open: cin, cout
  Multiplier #(.width(32)) multiplier_2 (.a(in_2), .b(in_4), .out(out_5), .cin(multiplier_1_out));  // open: cout

  // Other names for the same wires on the sheet: a00[31:0] = in_1; a01[31:0] = in_2; b00[31:0] = in_3;
  //   b10[31:0] = in_4
endmodule

module main (
  input  [31:0] in_1,
  output [31:0] out_2
);

  wire quick_pow_1_out_6;
  wire [31:0] mul1_1_out_7, quick_pow_1_out_7, quick_pow_1_out_8, quick_pow_1_out_9, quick_pow_1_out_10;

  quick_pow quick_pow_1 (
    .in_1({32{1'b0}}), .in_2(32'h1), .in_3(in_1), .in_4(32'h1), .in_5(32'h1), .out_6(quick_pow_1_out_6),
    .out_7(quick_pow_1_out_7), .out_8(quick_pow_1_out_8), .out_9(quick_pow_1_out_9),
    .out_10(quick_pow_1_out_10));
  mul1 mul1_1 (
    .in_1({32{1'b0}}), .in_2(32'h1), .in_3(quick_pow_1_out_7), .in_4(quick_pow_1_out_8),
    .in_5(quick_pow_1_out_9), .in_6(quick_pow_1_out_10), .out_7(mul1_1_out_7));  // open: out_8
  Multiplexer #(.width(32), .enable("false")) multiplexer_1 (
    .in0(mul1_1_out_7), .in1({32{1'b0}}), .out(out_2), .sel(quick_pow_1_out_6));
  // Probe on out_2
endmodule
