// Logisim project mod5.circ as structural Verilog: 1 circuit, main circuit mod5
module mod5 (
  input  in_1,
  output out_2,
  output out_3,
  output out_4,
  output out_5,
  output out_6
);

  wire clock_1_out;
  wire [1:1] register_1_q, register_1_q_2;

  Register #(.width(2)) register_1 (
    .D({register_1_q[1], in_1}), .Q({register_1_q_2[1], register_1_q[1]}), .clk(clock_1_out));  // open: en, clr
  Clock clock_1 (.out(clock_1_out));
  Decoder #(.select(2), .enable("false")) decoder_1 (
    .out0(out_3), .out1(out_4), .out2(out_6), .out3(out_5), .sel({register_1_q[1], in_1}));

  assign out_2 = 1'b0;
endmodule
